// Digital circuit main.dig as structural Verilog
module main (
);

  adder_8bit #(.applicationType("IVERILOG"), .CodeFile("/home/kaldwin/Development/Projects/the_electronics_project_misc/src/adder_8bit.v")) u_adder_8bit ();  // open: a, b, cin, sum, cout
endmodule
